// Logisim project 第一次数字逻辑实验.circ as structural Verilog
module \一位二进制半加器  (
  input  A,
  input  B,
  output S,
  output C
);

  wire nand_1_out, nand_2_out, nand_3_out;

  nand nand_1 (nand_1_out, A, B);
  not not_1 (C, nand_1_out);
  nand nand_2 (nand_2_out, A, nand_1_out);
  nand nand_3 (nand_3_out, nand_1_out, B);
  nand nand_4 (S, nand_2_out, nand_3_out);
endmodule

module \一位二进制全加器  (
  input  A,
  input  B,
  input  Ci_1,
  output Si,
  output Ci
);

  wire nand_1_out, nand_2_out, nand_3_out, xor_1_out;

  xor xor_1 (xor_1_out, A, B);
  nand nand_1 (nand_1_out, A, B);
  nand nand_2 (nand_2_out, A, Ci_1);
  nand nand_3 (nand_3_out, B, Ci_1);
  xor xor_2 (Si, xor_1_out, Ci_1);
  nand nand_4 (Ci, nand_1_out, nand_2_out, nand_3_out);
endmodule

module \串行4位二进制全加器  (
  input  A0,
  input  B0,
  input  C0,
  input  A1,
  input  B1,
  input  A2,
  input  B2,
  input  A3,
  input  B3,
  output S0,
  output S2,
  output S3,
  output S4,
  output C4
);

  wire nand_1_out, nand_2_out, nand_3_out, nand_4_out, nand_5_out, nand_6_out, nand_7_out, nand_8_out,
       nand_9_out, nand_10_out, nand_11_out, nand_12_out, nand_13_out, nand_14_out, nand_16_out, xor_1_out,
       xor_2_out, xor_3_out, xor_4_out;

  xor xor_1 (xor_1_out, A1, B1);
  xor xor_2 (xor_2_out, A2, B2);
  xor xor_3 (xor_3_out, A3, B3);
  xor xor_4 (xor_4_out, A0, B0);
  nand nand_1 (nand_1_out, A1, B1);
  nand nand_2 (nand_2_out, A1, nand_16_out);
  nand nand_3 (nand_3_out, B1, nand_16_out);
  nand nand_4 (nand_4_out, A2, B2);
  nand nand_5 (nand_5_out, A2, nand_13_out);
  nand nand_6 (nand_6_out, B2, nand_13_out);
  nand nand_7 (nand_7_out, A3, B3);
  nand nand_8 (nand_8_out, A3, nand_14_out);
  nand nand_9 (nand_9_out, B3, nand_14_out);
  nand nand_10 (nand_10_out, A0, B0);
  nand nand_11 (nand_11_out, A0, C0);
  nand nand_12 (nand_12_out, B0, C0);
  xor xor_5 (S2, xor_1_out, nand_16_out);
  xor xor_6 (S3, xor_2_out, nand_13_out);
  xor xor_7 (S4, xor_3_out, nand_14_out);
  xor xor_8 (S0, xor_4_out, C0);
  nand nand_13 (nand_13_out, nand_1_out, nand_2_out, nand_3_out);
  nand nand_14 (nand_14_out, nand_4_out, nand_5_out, nand_6_out);
  nand nand_15 (C4, nand_7_out, nand_8_out, nand_9_out);
  nand nand_16 (nand_16_out, nand_10_out, nand_11_out, nand_12_out);
endmodule

module \并行进位的串行二进制全加器  (
  input  C0,
  input  A0,
  input  B0,
  input  A1,
  input  B1,
  input  A2,
  input  B2,
  input  A3,
  input  B3,
  output S0,
  output S1,
  output C4,
  output S2,
  output S3
);

  wire and_1_out, and_2_out, and_3_out, and_4_out, and_5_out, and_6_out, and_7_out, and_8_out, and_9_out,
       and_10_out, C1_out, C2_out, C3_out, P0_out, P1_out, P2_out, P3_out, Q0_out, Q1_out, Q2_out, Q3_out,
       xor_1_out, xor_2_out, xor_5_out, xor_6_out;

  and P1 (P1_out, A1, B1);
  and P3 (P3_out, A3, B3);
  xor xor_1 (xor_1_out, A0, B0);
  and P0 (P0_out, A0, B0);
  and P2 (P2_out, A2, B2);
  or Q0 (Q0_out, A0, B0);
  or Q1 (Q1_out, A1, B1);
  or Q2 (Q2_out, A2, B2);
  or Q3 (Q3_out, A3, B3);
  and and_1 (and_1_out, C0, Q0_out);
  and and_2 (and_2_out, C0, Q0_out, Q1_out, Q2_out, Q3_out);
  and and_3 (and_3_out, P0_out, Q1_out, Q2_out, Q3_out);
  xor xor_2 (xor_2_out, A1, B1);
  xor xor_3 (S0, C0, xor_1_out);
  and and_4 (and_4_out, Q1_out, P0_out);
  and and_5 (and_5_out, P1_out, Q2_out, Q3_out);
  and and_6 (and_6_out, P2_out, Q3_out);
  and and_7 (and_7_out, Q2_out, Q1_out, Q0_out, C0);
  or C1 (C1_out, P0_out, and_1_out);
  and and_8 (and_8_out, Q0_out, C0, Q1_out);
  and and_9 (and_9_out, P1_out, Q2_out);
  and and_10 (and_10_out, Q2_out, Q1_out, P0_out);
  or or_1 (C4, and_2_out, and_3_out, and_5_out, and_6_out, P3_out);
  xor xor_4 (S1, xor_2_out, C1_out);
  or C2 (C2_out, and_8_out, P1_out, and_4_out);
  or C3 (C3_out, P2_out, and_9_out, and_10_out, and_7_out);
  xor xor_5 (xor_5_out, B2, A2);
  xor xor_6 (xor_6_out, A3, B3);
  xor xor_7 (S2, C2_out, xor_5_out);
  xor xor_8 (S3, C3_out, xor_6_out);
endmodule

module \封装  (
  input  in_1,
  input  in_2,
  input  in_3,
  input  in_4,
  input  in_5,
  input  in_6,
  input  in_7,
  input  in_8,
  input  in_9,
  output out_10,
  output out_11,
  output out_12,
  output out_13,
  output out_14
);

  \并行进位的串行二进制全加器  \u_并行进位的串行二进制全加器_1  (
    .C0(in_1), .A0(in_2), .B0(in_6), .A1(in_3), .B1(in_7), .A2(in_4), .B2(in_8), .A3(in_5), .B3(in_9),
    .S0(out_10), .S1(out_11), .C4(out_14), .S2(out_12), .S3(out_13));
endmodule

module _8421 (
  input  in_1,
  input  in_2,
  input  in_3,
  input  in_4,
  input  in_5,
  output out_6,
  output out_7,
  output out_8,
  output out_9,
  output out_10,
  output out_11,
  output out_12,
  output out_13,
  output out_14,
  output out_15
);

  wire and_1_out, or_1_out;

  or or_1 (or_1_out, in_2, in_3);
  and and_1 (and_1_out, in_4, or_1_out);
  \并行进位的串行二进制全加器  \u_并行进位的串行二进制全加器_1  (
    .C0(and_1_out), .A0(in_5), .B0(in_5), .A1(in_5), .B1(in_5), .A2(in_5), .B2(in_5), .A3(in_5), .B3(in_5),
    .S0(out_6), .S1(out_7), .C4(out_10), .S2(out_8), .S3(out_9));
  \并行进位的串行二进制全加器  \u_并行进位的串行二进制全加器_2  (
    .C0(in_5), .A0(in_1), .B0(in_5), .A1(in_2), .B1(and_1_out), .A2(in_3), .B2(and_1_out), .A3(in_4),
    .B3(in_5), .S0(out_11), .S1(out_12), .C4(out_15), .S2(out_13), .S3(out_14));
endmodule

module \_7段译码器  (
  input  in_1,
  input  in_2,
  input  in_3,
  input  in_4,
  input  in_5,
  input  in_6,
  input  in_7,
  input  in_8,
  input  in_9,
  input  in_10,
  input  in_11,
  input  in_12,
  input  in_13,
  input  in_14,
  input  in_15,
  input  in_16,
  input  in_17,
  output out_18,
  output out_19
);

  wire and_1_out, or_1_out, \并行进位的串行二进制全加器_1_s0 , \并行进位的串行二进制全加器_1_s1 , \并行进位的串行二进制全加器_1_s2 ,
       \并行进位的串行二进制全加器_1_s3 , \并行进位的串行二进制全加器_2_s0 , \并行进位的串行二进制全加器_2_s1 , \并行进位的串行二进制全加器_2_s2 ,
       \并行进位的串行二进制全加器_2_s3 , \测试姨妈管_1_a , \测试姨妈管_1_b , \测试姨妈管_1_c , \测试姨妈管_1_d , \测试姨妈管_1_e , \测试姨妈管_1_f ,
       \测试姨妈管_1_g , \测试姨妈管_2_a , \测试姨妈管_2_b , \测试姨妈管_2_c , \测试姨妈管_2_d , \测试姨妈管_2_e , \测试姨妈管_2_f , \测试姨妈管_2_g ;

  and and_1 (and_1_out, in_14, or_1_out);
  or or_1 (or_1_out, in_12, in_13);
  \并行进位的串行二进制全加器  \u_并行进位的串行二进制全加器_1  (
    .C0(and_1_out), .A0(in_1), .B0(in_5), .A1(in_2), .B1(in_6), .A2(in_3), .B2(in_7), .A3(in_4), .B3(in_8),
    .S0(\并行进位的串行二进制全加器_1_s0 ), .S1(\并行进位的串行二进制全加器_1_s1 ), .C4(out_18), .S2(\并行进位的串行二进制全加器_1_s2 ),
    .S3(\并行进位的串行二进制全加器_1_s3 ));
  \并行进位的串行二进制全加器  \u_并行进位的串行二进制全加器_2  (
    .C0(in_10), .A0(in_11), .B0(in_15), .A1(in_12), .B1(and_1_out), .A2(in_13), .B2(and_1_out), .A3(in_14),
    .B3(in_16), .S0(\并行进位的串行二进制全加器_2_s0 ), .S1(\并行进位的串行二进制全加器_2_s1 ), .C4(out_19), .S2(\并行进位的串行二进制全加器_2_s2 ),
    .S3(\并行进位的串行二进制全加器_2_s3 ));
  \测试姨妈管  \u_测试姨妈管_1  (
    .S3(\并行进位的串行二进制全加器_1_s3 ), .S2(\并行进位的串行二进制全加器_1_s2 ), .S1(\并行进位的串行二进制全加器_1_s1 ),
    .S0(\并行进位的串行二进制全加器_1_s0 ), .a(\测试姨妈管_1_a ), .b(\测试姨妈管_1_b ), .c(\测试姨妈管_1_c ), .d(\测试姨妈管_1_d ),
    .e(\测试姨妈管_1_e ), .f(\测试姨妈管_1_f ), .g(\测试姨妈管_1_g ));
  \测试姨妈管  \u_测试姨妈管_2  (
    .S3(\并行进位的串行二进制全加器_2_s3 ), .S2(\并行进位的串行二进制全加器_2_s2 ), .S1(\并行进位的串行二进制全加器_2_s1 ),
    .S0(\并行进位的串行二进制全加器_2_s0 ), .a(\测试姨妈管_2_a ), .b(\测试姨妈管_2_b ), .c(\测试姨妈管_2_c ), .d(\测试姨妈管_2_d ),
    .e(\测试姨妈管_2_e ), .f(\测试姨妈管_2_f ), .g(\测试姨妈管_2_g ));
  _7_Segment_Display u_7_segment_display_1 (
    .g(\测试姨妈管_1_g ), .f(\测试姨妈管_1_a ), .a(\测试姨妈管_1_b ), .b(\测试姨妈管_1_c ), .e(\测试姨妈管_1_f ), .d(\测试姨妈管_1_e ),
    .c(\测试姨妈管_1_d ), .dp(in_9));
  _7_Segment_Display u_7_segment_display_2 (
    .g(\测试姨妈管_2_g ), .f(\测试姨妈管_2_a ), .a(\测试姨妈管_2_b ), .b(\测试姨妈管_2_c ), .e(\测试姨妈管_2_f ), .d(\测试姨妈管_2_e ),
    .c(\测试姨妈管_2_d ), .dp(in_17));
endmodule

module \测试姨妈管  (
  input  S3,
  input  S2,
  input  S1,
  input  S0,
  output a,
  output b,
  output c,
  output d,
  output e,
  output f,
  output g
);

  wire and_1_out, and_2_out, and_3_out, and_4_out, and_5_out, and_6_out, and_7_out, and_8_out, and_9_out,
       and_10_out, and_11_out, and_12_out, and_13_out, and_14_out, and_15_out, and_16_out, and_17_out,
       and_18_out, and_19_out, and_20_out, and_21_out, and_22_out, and_23_out, and_24_out, and_25_out,
       and_26_out, not_1_out, not_2_out, not_3_out, not_4_out, not_5_out, not_6_out, not_7_out, not_8_out,
       not_9_out, not_10_out, not_11_out, not_12_out, not_13_out, not_14_out, not_15_out, not_16_out,
       not_17_out, not_18_out, not_19_out, not_20_out, not_21_out, not_22_out, not_23_out, not_24_out,
       not_25_out, not_26_out, not_27_out, not_28_out, not_29_out, not_30_out, not_31_out, not_32_out,
       not_33_out, not_34_out, not_35_out, not_36_out, not_37_out, not_38_out, not_39_out, not_40_out,
       not_41_out, not_42_out, not_43_out, not_44_out, not_45_out, not_46_out, not_47_out, not_48_out,
       not_49_out, not_50_out, not_51_out, not_52_out;

  not not_1 (not_1_out, S3);
  not not_2 (not_2_out, S1);
  and and_1 (and_1_out, not_1_out, not_2_out, not_3_out);
  not not_3 (not_3_out, S0);
  not not_4 (not_4_out, S3);
  and and_2 (and_2_out, not_4_out, S2, not_5_out);
  not not_5 (not_5_out, S1);
  not not_6 (not_6_out, S3);
  and and_3 (and_3_out, not_6_out, S2, not_7_out);
  not not_7 (not_7_out, S0);
  and and_4 (and_4_out, S3, not_8_out, not_9_out);
  not not_8 (not_8_out, S2);
  not not_9 (not_9_out, S1);
  not not_10 (not_10_out, S3);
  not not_11 (not_11_out, S2);
  and and_5 (and_5_out, not_10_out, not_11_out, not_12_out);
  not not_12 (not_12_out, S0);
  not not_13 (not_13_out, S3);
  and and_6 (and_6_out, not_13_out, S1);
  not not_14 (not_14_out, S3);
  and and_7 (and_7_out, not_14_out, S2, S0);
  not not_15 (not_15_out, S2);
  and and_8 (and_8_out, S3, not_15_out, not_16_out);
  not not_16 (not_16_out, S1);
  not not_17 (not_17_out, S3);
  and and_9 (and_9_out, not_17_out, not_18_out);
  not not_18 (not_18_out, S2);
  not not_19 (not_19_out, S3);
  not not_20 (not_20_out, S1);
  and and_10 (and_10_out, not_19_out, not_20_out, not_21_out);
  not not_21 (not_21_out, S0);
  not not_22 (not_22_out, S2);
  and and_11 (and_11_out, not_22_out, not_23_out);
  not not_23 (not_23_out, S1);
  not not_24 (not_24_out, S3);
  and and_12 (and_12_out, not_24_out, S1, S0);
  not not_25 (not_25_out, S2);
  and and_13 (and_13_out, not_25_out, not_26_out);
  not not_26 (not_26_out, S1);
  not not_27 (not_27_out, S3);
  and and_14 (and_14_out, not_27_out, S0);
  not not_28 (not_28_out, S3);
  and and_15 (and_15_out, not_28_out, S2);
  not not_29 (not_29_out, S3);
  not not_30 (not_30_out, S2);
  not not_31 (not_31_out, S0);
  not not_32 (not_32_out, S3);
  not not_33 (not_33_out, S2);
  not not_34 (not_34_out, S3);
  not not_35 (not_35_out, S0);
  not not_36 (not_36_out, S3);
  not not_37 (not_37_out, S1);
  not not_38 (not_38_out, S2);
  not not_39 (not_39_out, S1);
  not not_40 (not_40_out, S2);
  and and_16 (and_16_out, not_40_out, not_41_out, not_42_out);
  not not_41 (not_41_out, S1);
  not not_42 (not_42_out, S0);
  not not_43 (not_43_out, S3);
  and and_17 (and_17_out, not_43_out, S1, not_44_out);
  not not_44 (not_44_out, S0);
  not not_45 (not_45_out, S3);
  and and_18 (and_18_out, not_45_out, not_46_out, S1);
  not not_46 (not_46_out, S2);
  not not_47 (not_47_out, S3);
  and and_19 (and_19_out, not_47_out, S2, not_48_out);
  not not_48 (not_48_out, S1);
  not not_49 (not_49_out, S3);
  and and_20 (and_20_out, not_49_out, S2, not_50_out);
  not not_50 (not_50_out, S0);
  and and_21 (and_21_out, S3, not_51_out, not_52_out);
  not not_51 (not_51_out, S2);
  not not_52 (not_52_out, S1);
  or or_1 (a, and_1_out, and_2_out, and_3_out, and_4_out);
  or or_2 (b, and_5_out, and_6_out, and_7_out, and_8_out);
  or or_3 (c, and_9_out, and_10_out, and_11_out, and_12_out);
  or or_4 (d, and_13_out, and_14_out, and_15_out);
  and and_22 (and_22_out, not_29_out, not_30_out, not_31_out);
  and and_23 (and_23_out, not_32_out, not_33_out, S1);
  and and_24 (and_24_out, not_34_out, S1, not_35_out);
  and and_25 (and_25_out, not_36_out, S2, not_37_out, S0);
  and and_26 (and_26_out, S3, not_38_out, not_39_out);
  or or_5 (f, and_16_out, and_17_out);
  or or_6 (g, and_18_out, and_19_out, and_20_out, and_21_out);
  or or_7 (e, and_22_out, and_23_out, and_24_out, and_25_out, and_26_out);
endmodule

module \四位二进制可逆计数器  (
  input  CPu,
  input  CLR,
  input  CPd,
  output out_4,
  output out_5,
  output out_6,
  output out_7
);

  wire and_1_out, and_2_out, and_3_out, and_4_out, and_5_out, and_6_out, and_7_out, and_8_out, and_9_out,
       and_10_out, and_11_out, and_12_out, and_13_out, and_14_out, and_15_out, and_16_out, and_17_out,
       and_18_out, and_19_out, and_20_out, and_21_out, and_22_out, and_23_out, and_24_out, and_25_out,
       and_26_out, and_27_out, and_28_out, not_1_out, not_2_out, not_3_out, not_4_out, not_5_out, not_6_out,
       not_7_out, not_8_out, not_9_out, not_10_out, not_11_out, not_12_out, not_13_out, not_14_out,
       not_15_out, not_16_out, not_17_out, not_18_out, not_19_out, not_20_out, not_21_out, not_22_out,
       not_23_out, not_24_out, not_25_out, not_26_out, not_27_out, not_28_out, not_29_out, not_30_out,
       not_31_out, not_32_out, not_33_out, not_34_out, not_35_out, not_36_out, not_37_out, not_38_out,
       not_39_out, or_1_out, or_2_out, or_3_out, or_4_out, or_5_out;

  not not_1 (not_1_out, CPu);
  not not_2 (not_2_out, CLR);
  not not_3 (not_3_out, out_4);
  not not_4 (not_4_out, out_5);
  not not_5 (not_5_out, out_6);
  not not_6 (not_6_out, out_7);
  not not_7 (not_7_out, CLR);
  not not_8 (not_8_out, CLR);
  not not_9 (not_9_out, CLR);
  not not_10 (not_10_out, out_4);
  not not_11 (not_11_out, CPu);
  not not_12 (not_12_out, CLR);
  not not_13 (not_13_out, out_5);
  not not_14 (not_14_out, out_6);
  not not_15 (not_15_out, out_7);
  not not_16 (not_16_out, CLR);
  not not_17 (not_17_out, CLR);
  not not_18 (not_18_out, CLR);
  not not_19 (not_19_out, out_5);
  not not_20 (not_20_out, out_6);
  not not_21 (not_21_out, out_7);
  not not_22 (not_22_out, out_5);
  not not_23 (not_23_out, CPu);
  not not_24 (not_24_out, CLR);
  not not_25 (not_25_out, out_6);
  not not_26 (not_26_out, out_7);
  not not_27 (not_27_out, CLR);
  not not_28 (not_28_out, out_6);
  not not_29 (not_29_out, out_7);
  not not_30 (not_30_out, CLR);
  not not_31 (not_31_out, CLR);
  not not_32 (not_32_out, CLR);
  not not_33 (not_33_out, out_7);
  not not_34 (not_34_out, out_7);
  or or_1 (or_1_out, CPd, CLR, CPu);
  and and_1 (and_1_out, not_1_out, not_2_out, CPd, not_3_out, not_4_out, not_5_out, not_6_out);
  and and_2 (and_2_out, not_7_out, CPd, out_4, out_7);
  and and_3 (and_3_out, not_8_out, CPd, out_4, out_6);
  and and_4 (and_4_out, not_9_out, CPd, out_4, out_5);
  and and_5 (and_5_out, CPu, not_10_out, out_5, out_6, out_7);
  and and_6 (and_6_out, CPu, out_4, not_35_out);
  not not_35 (not_35_out, out_5);
  and and_7 (and_7_out, CPu, out_4, not_36_out);
  not not_36 (not_36_out, out_6);
  and and_8 (and_8_out, CPu, out_4, not_37_out);
  not not_37 (not_37_out, out_7);
  and and_9 (and_9_out, CPu, CLR, out_4);
  and and_10 (and_10_out, not_11_out, not_12_out, CPd, not_13_out, not_14_out, not_15_out);
  and and_11 (and_11_out, not_16_out, CPd, out_5, out_7);
  and and_12 (and_12_out, not_17_out, CPd, out_5, out_6);
  and and_13 (and_13_out, not_18_out, CPd, out_4, not_19_out, not_20_out, not_21_out);
  and and_14 (and_14_out, CPu, not_22_out, out_6, out_7);
  and and_15 (and_15_out, CPu, out_5, not_38_out);
  not not_38 (not_38_out, out_6);
  and and_16 (and_16_out, CPu, out_5, not_39_out);
  not not_39 (not_39_out, out_7);
  and and_17 (and_17_out, CPu, CLR, out_4, out_5);
  and and_18 (and_18_out, not_23_out, not_24_out, CPd, not_25_out, not_26_out);
  and and_19 (and_19_out, not_27_out, CPd, out_6, out_7);
  and and_20 (and_20_out, CPu, not_28_out, out_7);
  and and_21 (and_21_out, CPu, out_6, not_29_out);
  and and_22 (and_22_out, CPu, not_30_out, CPd, out_5);
  and and_23 (and_23_out, CPu, not_31_out, CPd, out_4);
  and and_24 (and_24_out, CPu, CLR, out_4, out_5, out_6);
  and and_25 (and_25_out, not_32_out, CPd, not_33_out);
  and and_26 (and_26_out, CPu, not_34_out);
  and and_27 (and_27_out, CPu, CPd, out_4, out_5, out_6);
  and and_28 (and_28_out, CPu, CLR, out_4, out_5, out_6);
  or or_2 (or_2_out, and_18_out, and_19_out, and_20_out, and_21_out, and_22_out, and_23_out, and_24_out);
  or or_3 (or_3_out, and_25_out, and_26_out, and_27_out, and_28_out);
  or or_4 (or_4_out, and_1_out, and_2_out, and_3_out, and_4_out, and_5_out, and_6_out, and_7_out, and_8_out, and_9_out);
  or or_5 (or_5_out, and_10_out, and_11_out, and_12_out, and_13_out, and_14_out, and_15_out, and_16_out, and_17_out);
  D_Flip_Flop #(.trigger("falling")) d_ff_1 (.clk(or_1_out), .D(or_4_out), .Q(out_4));  // open: Qn, preset, en, reset
  D_Flip_Flop #(.trigger("falling")) d_ff_2 (.clk(or_1_out), .D(or_5_out), .Q(out_5));  // open: Qn, preset, en, reset
  D_Flip_Flop #(.trigger("falling")) d_ff_3 (.clk(or_1_out), .D(or_2_out), .Q(out_6));  // open: Qn, preset, en, reset
  D_Flip_Flop #(.trigger("falling")) d_ff_4 (.clk(or_1_out), .D(or_3_out), .Q(out_7));  // open: Qn, preset, en, reset
endmodule

module \报警  (
  input  in_1,
  input  in_2,
  input  in_3,
  output out_4,
  output out_5,
  output out_6,
  output out_7
);

  wire and_1_out, and_2_out, d_ff_1_q, d_ff_2_q, d_ff_3_q, d_ff_4_q;

  \_4位二进制可逆计数器  \u_4位二进制可逆计数器_1  (.CLu(in_1), .CLR(in_2), .CPd(in_3), .Qa(out_4), .Qb(out_5), .Qc(out_6), .Qd(out_7));
  and and_1 (and_1_out, and_2_out, out_4, out_5, out_6, out_7);
  D_Flip_Flop d_ff_1 (.clk(in_1), .D(out_7), .Q(d_ff_1_q));  // open: Qn, preset, en, reset
  D_Flip_Flop d_ff_2 (.clk(in_1), .D(out_6), .Q(d_ff_2_q));  // open: Qn, preset, en, reset
  D_Flip_Flop d_ff_3 (.clk(in_1), .D(out_5), .Q(d_ff_3_q));  // open: Qn, preset, en, reset
  D_Flip_Flop d_ff_4 (.clk(in_1), .D(out_4), .Q(d_ff_4_q));  // open: Qn, preset, en, reset
  LED \u_报警器  (.in(and_1_out));
  and and_2 (and_2_out, d_ff_1_q, d_ff_2_q, d_ff_3_q, d_ff_4_q);
endmodule

module \实验2封装  (
  input  in_1,
  input  in_2,
  input  in_3,
  input  in_4,
  output out_5,
  output out_6,
  output out_7,
  output out_8,
  output out_9,
  output out_10,
  output out_11,
  output out_12,
  output out_13,
  output out_14,
  output out_15,
  output out_16,
  output out_17,
  output out_18,
  output out_19
);

  wire and_2_out, d_ff_1_q, d_ff_2_q, d_ff_3_q, d_ff_4_q, \n4位二进制可逆计数器_1_qa , \n4位二进制可逆计数器_1_qb ,
       \n4位二进制可逆计数器_1_qc , \n4位二进制可逆计数器_1_qd , n8421_1_out_6, n8421_1_out_7, n8421_1_out_8, n8421_1_out_9,
       n8421_1_out_11, n8421_1_out_12, n8421_1_out_13, n8421_1_out_14;

  \_4位二进制可逆计数器  \u_4位二进制可逆计数器_1  (
    .CLu(in_2), .CLR(in_3), .CPd(in_4), .Qa(\n4位二进制可逆计数器_1_qa ), .Qb(\n4位二进制可逆计数器_1_qb ),
    .Qc(\n4位二进制可逆计数器_1_qc ), .Qd(\n4位二进制可逆计数器_1_qd ));
  D_Flip_Flop d_ff_1 (.clk(in_2), .D(\n4位二进制可逆计数器_1_qa ), .Q(d_ff_1_q));  // open: Qn, preset, en, reset
  D_Flip_Flop d_ff_2 (.clk(in_2), .D(\n4位二进制可逆计数器_1_qb ), .Q(d_ff_2_q));  // open: Qn, preset, en, reset
  D_Flip_Flop d_ff_3 (.clk(in_2), .D(\n4位二进制可逆计数器_1_qc ), .Q(d_ff_3_q));  // open: Qn, preset, en, reset
  D_Flip_Flop d_ff_4 (.clk(in_2), .D(\n4位二进制可逆计数器_1_qd ), .Q(d_ff_4_q));  // open: Qn, preset, en, reset
  and and_1 (out_5, and_2_out, \n4位二进制可逆计数器_1_qa , \n4位二进制可逆计数器_1_qb , \n4位二进制可逆计数器_1_qc , \n4位二进制可逆计数器_1_qd );
  and and_2 (and_2_out, d_ff_1_q, d_ff_2_q, d_ff_3_q, d_ff_4_q);
  _8421 u_8421_1 (
    .in_1(\n4位二进制可逆计数器_1_qd ), .in_2(\n4位二进制可逆计数器_1_qc ), .in_3(\n4位二进制可逆计数器_1_qb ),
    .in_4(\n4位二进制可逆计数器_1_qa ), .out_6(n8421_1_out_6), .out_7(n8421_1_out_7), .out_8(n8421_1_out_8),
    .out_9(n8421_1_out_9), .out_12(n8421_1_out_12), .out_13(n8421_1_out_13), .out_14(n8421_1_out_14),
    .out_11(n8421_1_out_11), .in_5(in_1));  // open: out_15, out_10
  \测试姨妈管  \u_测试姨妈管_1  (
    .S3(n8421_1_out_9), .S2(n8421_1_out_8), .S1(n8421_1_out_7), .S0(n8421_1_out_6), .a(out_6), .b(out_7),
    .c(out_8), .d(out_9), .e(out_10), .f(out_11), .g(out_12));
  \测试姨妈管  \u_测试姨妈管_2  (
    .S3(n8421_1_out_14), .S2(n8421_1_out_13), .S1(n8421_1_out_12), .S0(n8421_1_out_11), .a(out_13),
    .b(out_14), .c(out_15), .d(out_16), .e(out_17), .f(out_18), .g(out_19));
endmodule

module \封装测试  (
  input  in_1
);

  wire button_1_out, button_2_out, button_3_out, \实验2封装_1_out_5 , \实验2封装_1_out_6 , \实验2封装_1_out_7 ,
       \实验2封装_1_out_8 , \实验2封装_1_out_9 , \实验2封装_1_out_10 , \实验2封装_1_out_11 , \实验2封装_1_out_12 ,
       \实验2封装_1_out_13 , \实验2封装_1_out_14 , \实验2封装_1_out_15 , \实验2封装_1_out_16 , \实验2封装_1_out_17 ,
       \实验2封装_1_out_18 , \实验2封装_1_out_19 ;

  Button button_1 (.out(button_1_out));
  Button button_2 (.out(button_2_out));
  Button button_3 (.out(button_3_out));
  LED led_1 (.in(\实验2封装_1_out_5 ));
  \实验2封装  \u_实验2封装_1  (
    .in_3(button_2_out), .in_4(button_3_out), .out_5(\实验2封装_1_out_5 ), .out_6(\实验2封装_1_out_6 ),
    .out_7(\实验2封装_1_out_7 ), .out_8(\实验2封装_1_out_8 ), .out_9(\实验2封装_1_out_9 ), .out_10(\实验2封装_1_out_10 ),
    .out_11(\实验2封装_1_out_11 ), .out_12(\实验2封装_1_out_12 ), .out_13(\实验2封装_1_out_13 ),
    .out_14(\实验2封装_1_out_14 ), .out_15(\实验2封装_1_out_15 ), .out_16(\实验2封装_1_out_16 ),
    .out_17(\实验2封装_1_out_17 ), .out_18(\实验2封装_1_out_18 ), .out_19(\实验2封装_1_out_19 ), .in_1(in_1),
    .in_2(button_1_out));
  _7_Segment_Display u_7_segment_display_1 (
    .g(\实验2封装_1_out_12 ), .f(\实验2封装_1_out_6 ), .a(\实验2封装_1_out_7 ), .b(\实验2封装_1_out_8 ),
    .e(\实验2封装_1_out_11 ), .d(\实验2封装_1_out_10 ), .c(\实验2封装_1_out_9 ));  // open: dp
  _7_Segment_Display u_7_segment_display_2 (
    .g(\实验2封装_1_out_19 ), .f(\实验2封装_1_out_13 ), .a(\实验2封装_1_out_14 ), .b(\实验2封装_1_out_15 ),
    .e(\实验2封装_1_out_18 ), .d(\实验2封装_1_out_17 ), .c(\实验2封装_1_out_16 ));  // open: dp
endmodule

module \_4位二进制可逆计数器  (
  input  CLu,
  input  CLR,
  input  CPd,
  output Qa,
  output Qb,
  output Qc,
  output Qd
);

  wire and_1_out, and_2_out, and_3_out, and_4_out, and_5_out, and_6_out, and_7_out, and_8_out, and_9_out,
       and_10_out, and_11_out, and_12_out, and_13_out, and_14_out, and_15_out, and_16_out, and_17_out,
       and_18_out, and_19_out, and_20_out, and_21_out, and_22_out, and_23_out, and_24_out, and_25_out,
       and_26_out, and_27_out, and_28_out, and_29_out, and_30_out, and_31_out, not_1_out, not_2_out,
       not_3_out, not_4_out, not_5_out, not_6_out, not_7_out, not_8_out, not_9_out, not_10_out, not_11_out,
       not_12_out, not_13_out, not_14_out, not_15_out, not_16_out, not_17_out, not_18_out, not_19_out,
       not_20_out, not_21_out, not_22_out, not_23_out, not_24_out, not_25_out, not_26_out, not_27_out,
       not_28_out, not_29_out, not_30_out, not_31_out, not_32_out, or_1_out, or_2_out, or_3_out, or_4_out,
       or_5_out;

  not not_1 (not_1_out, CLR);
  not not_2 (not_2_out, CLR);
  not not_3 (not_3_out, CLR);
  not not_4 (not_4_out, CLR);
  not not_5 (not_5_out, CLR);
  not not_6 (not_6_out, CLR);
  not not_7 (not_7_out, Qb);
  not not_8 (not_8_out, Qc);
  not not_9 (not_9_out, Qd);
  not not_10 (not_10_out, Qb);
  not not_11 (not_11_out, CLR);
  not not_12 (not_12_out, CLR);
  not not_13 (not_13_out, Qc);
  not not_14 (not_14_out, Qd);
  not not_15 (not_15_out, CLR);
  not not_16 (not_16_out, Qc);
  not not_17 (not_17_out, Qd);
  not not_18 (not_18_out, Qc);
  not not_19 (not_19_out, Qd);
  not not_20 (not_20_out, CLR);
  not not_21 (not_21_out, Qd);
  not not_22 (not_22_out, CLR);
  not not_23 (not_23_out, Qd);
  not not_24 (not_24_out, CLR);
  not not_25 (not_25_out, Qd);
  not not_26 (not_26_out, Qd);
  not not_27 (not_27_out, Qa);
  not not_28 (not_28_out, Qb);
  not not_29 (not_29_out, Qc);
  not not_30 (not_30_out, Qd);
  and and_1 (and_1_out, not_1_out, CPd, Qa, Qd);
  and and_2 (and_2_out, not_2_out, CPd, Qa, Qc);
  and and_3 (and_3_out, not_3_out, CPd, Qa, Qb);
  and and_4 (and_4_out, CLu, Qb, Qc, Qd);
  and and_5 (and_5_out, CLu, Qa);
  and and_6 (and_6_out, not_4_out, CPd, Qb, Qd);
  and and_7 (and_7_out, not_5_out, CPd, Qb, Qc);
  and and_8 (and_8_out, not_6_out, CPd, Qa, not_7_out, not_8_out, not_9_out);
  and and_9 (and_9_out, CLu, not_10_out, Qc, Qd);
  and and_10 (and_10_out, CLu, Qb, not_31_out);
  not not_31 (not_31_out, Qc);
  and and_11 (and_11_out, CLu, Qb, not_32_out);
  not not_32 (not_32_out, Qd);
  and and_12 (and_12_out, CLu, Qa, Qb);
  and and_13 (and_13_out, not_11_out, CPd, Qc, Qd);
  and and_14 (and_14_out, not_12_out, CPd, Qb, not_13_out, not_14_out);
  and and_15 (and_15_out, not_15_out, CPd, Qa, not_16_out, not_17_out);
  and and_16 (and_16_out, CLu, not_18_out, Qd);
  and and_17 (and_17_out, CLu, Qc, not_19_out);
  and and_18 (and_18_out, CLu, Qa, Qb, Qc);
  and and_19 (and_19_out, not_20_out, CPd, Qc, not_21_out);
  and and_20 (and_20_out, not_22_out, CPd, Qb, not_23_out);
  and and_21 (and_21_out, not_24_out, CPd, Qa, not_25_out);
  and and_22 (and_22_out, CLu, not_26_out);
  and and_23 (and_23_out, CLu, Qa, Qb, Qc);
  and and_24 (and_24_out, CPd, Qd);
  and and_25 (and_25_out, CPd, Qc);
  and and_26 (and_26_out, CPd, Qb);
  and and_27 (and_27_out, CPd, Qa);
  and and_28 (and_28_out, CLu, not_27_out);
  and and_29 (and_29_out, CLu, not_28_out);
  and and_30 (and_30_out, CLu, not_29_out);
  and and_31 (and_31_out, CLu, not_30_out);
  or or_1 (or_1_out, and_1_out, and_2_out, and_3_out, and_4_out, and_5_out);
  or or_2 (or_2_out, and_6_out, and_7_out, and_8_out, and_9_out, and_10_out, and_11_out, and_12_out);
  or or_3 (or_3_out, and_13_out, and_14_out, and_15_out, and_16_out, and_17_out, and_18_out);
  or or_4 (or_4_out, and_19_out, and_20_out, and_21_out, and_22_out, and_23_out);
  or or_5 (or_5_out, and_24_out, and_25_out, and_26_out, and_27_out, CLR, and_28_out, and_29_out, and_30_out, and_31_out);
  D_Flip_Flop d_ff_1 (.clk(or_5_out), .D(or_1_out), .Q(Qa));  // open: Qn, preset, en, reset
  D_Flip_Flop d_ff_2 (.clk(or_5_out), .D(or_2_out), .Q(Qb));  // open: Qn, preset, en, reset
  D_Flip_Flop d_ff_3 (.clk(or_5_out), .D(or_3_out), .Q(Qc));  // open: Qn, preset, en, reset
  D_Flip_Flop d_ff_4 (.clk(or_5_out), .D(or_4_out), .Q(Qd));  // open: Qn, preset, en, reset
endmodule

module \封装测试可逆加法器  (
  input  in_1,
  input  in_2,
  input  in_3,
  output out_4,
  output out_5,
  output out_6,
  output out_7
);

  \四位二进制可逆计数器  \u_四位二进制可逆计数器_1  (
    .CPu(in_1), .CLR(in_2), .CPd(in_3), .out_4(out_4), .out_5(out_5), .out_6(out_6), .out_7(out_7));
endmodule

module \_8421测试  (
  input  in_1,
  input  in_2,
  input  in_3,
  input  in_4,
  input  in_5,
  output out_6,
  output out_7,
  output out_8,
  output out_9,
  output out_10,
  output out_11,
  output out_12,
  output out_13,
  output out_14,
  output out_15
);

  _8421 u_8421_1 (
    .in_1(in_2), .in_2(in_3), .in_3(in_4), .in_4(in_5), .out_6(out_6), .out_7(out_7), .out_8(out_8),
    .out_9(out_9), .out_12(out_12), .out_13(out_13), .out_14(out_14), .out_11(out_11), .in_5(in_1),
    .out_15(out_15), .out_10(out_10));
endmodule
